// Logisim project lab14.circ as structural Verilog: 1 circuit, main circuit main
module main (
  input  R,
  input  S,
  input  C,
  input  J,
  input  S_2,
  input  R_2,
  input  C_2,
  input  K,
  input  nS,
  input  S_3,
  input  in_11,
  input  C_3,
  input  nS_2,
  input  J_2,
  input  R_3,
  input  nR,
  input  C_4,
  input  nS_3,
  input  K_2,
  input  nR_2,
  input  C_5,
  input  nR_3,
  output Q,
  output Q_2,
  output Q_3,
  output nQ,
  output nQ_2,
  output nQ_3,
  output Q_4,
  output nQ_4,
  output Q_5,
  output nQ_5,
  output Q_6,
  output nQ_6
);

  wire nand_1_out, nand_2_out, nand_3_out, nand_4_out, nand_5_out, nand_6_out, nand_7_out, nand_8_out,
       nand_9_out, nand_12_out, nand_13_out, nand_14_out, nand_15_out, nand_20_out, nand_21_out, nand_22_out,
       nand_23_out, nand_24_out, nand_25_out, nand_26_out, nand_27_out, nand_28_out, nand_29_out,
       nand_30_out, nand_31_out, nor_3_out;

  nor nor_1 (Q, R, nQ_2);
  nor nor_2 (nQ_2, Q, S_2);
  nand nand_1 (nand_1_out, C_3, C_3);
  nand nand_2 (nand_2_out, nS_3, nand_3_out);
  nand nand_3 (nand_3_out, nand_2_out, C_5, nand_4_out);
  nand nand_4 (nand_4_out, nand_3_out, C_5, nand_5_out);
  nand nand_5 (nand_5_out, nand_4_out, nR_3);
  nand nand_6 (nand_6_out, S_3, nand_1_out);
  nand nand_7 (nand_7_out, nand_1_out, R_3);
  nand nand_8 (nand_8_out, nS, nand_6_out, nand_9_out);
  nand nand_9 (nand_9_out, nand_8_out, nand_7_out, nR);
  nand nand_10 (Q_6, nQ_6, nand_3_out);
  nand nand_11 (nQ_6, nand_4_out, Q_6);
  nand nand_12 (nand_12_out, S, C);
  nand nand_13 (nand_13_out, C, R_2);
  nand nand_14 (nand_14_out, nand_8_out, C_3);
  nand nand_15 (nand_15_out, C_3, nand_9_out);
  nand nand_16 (Q_2, nand_12_out, nQ);
  nand nand_17 (nQ, Q_2, nand_13_out);
  nand nand_18 (Q_4, nS, nand_14_out, nQ_4);
  nand nand_19 (nQ_4, Q_4, nand_15_out, nR);
  nand nand_20 (nand_20_out, nQ_5, J_2, C_4);
  nand nand_21 (nand_21_out, C_4, K_2, Q_5);
  nand nand_22 (nand_22_out, nQ_3, J, C_2);
  nand nand_23 (nand_23_out, C_2, K, Q_3);
  nor nor_3 (nor_3_out, C_2, C_2);
  nand nand_24 (nand_24_out, nand_22_out, nand_25_out);
  nand nand_25 (nand_25_out, nand_24_out, nand_23_out);
  nand nand_26 (nand_26_out, nS_2, nand_20_out, nand_27_out);
  nand nand_27 (nand_27_out, nand_26_out, nand_21_out, nR_2);
  nand nand_28 (nand_28_out, nand_20_out, nand_26_out, nand_21_out);
  nand nand_29 (nand_29_out, nand_21_out, nand_27_out, nand_20_out);
  nand nand_30 (nand_30_out, nand_24_out, nor_3_out);
  nand nand_31 (nand_31_out, nor_3_out, nand_25_out);
  nand nand_32 (Q_3, nQ_3, nand_30_out);
  nand nand_33 (nQ_3, nand_31_out, Q_3);
  nand nand_34 (Q_5, nS_2, nand_28_out, nQ_5);
  nand nand_35 (nQ_5, Q_5, nand_29_out, nR_2);

  // Notes on the sheet:
  //   ASYNC RS-T OR-NOT
  //   SYNC RS-T DYN-HNDL
  //   SYNC 2-ST STAT RS-T ASYNC-IN
  //   SYNC STAT RS-T
  //   SYNC 2-ST JK-T ASYNC-IN
  //   SYNC 2-ST JK-T
endmodule
